// Logisim project serialX_serialY_multiplier_8bit.circ as structural Verilog: 1 circuit, main circuit main
module main (
  input  Serial_Multiplicand,
  input  Serial_Multiplier
);

  wire adder_1_cout, adder_1_out, adder_2_cout, adder_2_out, adder_3_cout, adder_3_out, adder_4_cout,
       adder_4_out, adder_5_cout, adder_5_out, adder_6_cout, adder_6_out, adder_7_cout, adder_7_out,
       and_1_out, and_2_out, and_3_out, and_4_out, and_5_out, and_6_out, and_7_out, and_8_out, CLK_out,
       d_ff_1_q, d_ff_2_q, d_ff_3_q, d_ff_4_q, d_ff_5_q, d_ff_6_q, d_ff_7_q, d_ff_8_q, d_ff_9_q, d_ff_10_q,
       d_ff_11_q, d_ff_12_q, d_ff_13_q, d_ff_14_q, d_ff_15_q, d_ff_16_q, d_ff_17_q, d_ff_18_q, d_ff_19_q,
       d_ff_20_q, d_ff_21_q, d_ff_22_q, d_ff_23_q, d_ff_24_q, d_ff_25_q, d_ff_26_q, d_ff_27_q, d_ff_28_q,
       d_ff_29_q, d_ff_30_q, d_ff_31_q, d_ff_32_q, d_ff_33_q, d_ff_34_q, d_ff_35_q, d_ff_36_q, d_ff_37_q,
       d_ff_38_q, d_ff_39_q, d_ff_40_q, d_ff_41_q, d_ff_42_q, d_ff_43_q, d_ff_44_q, d_ff_45_q, d_ff_46_q,
       d_ff_47_q, d_ff_48_q, d_ff_49_q, d_ff_50_q, d_ff_51_q, d_ff_52_q, d_ff_53_q, d_ff_54_q, d_ff_55_q,
       d_ff_56_q, d_ff_57_q, d_ff_58_q, d_ff_59_q, d_ff_60_q, d_ff_61_q, d_ff_62_q, d_ff_63_q, d_ff_64_q,
       d_ff_65_q, d_ff_66_q, d_ff_67_q, d_ff_68_q, d_ff_69_q, d_ff_70_q, d_ff_71_q;

  Clock CLK (.out(CLK_out));
  D_Flip_Flop d_ff_1 (.clk(CLK_out), .D(Serial_Multiplicand), .Q(d_ff_1_q));  // open: Qn, preset, en, reset
  D_Flip_Flop d_ff_2 (.clk(CLK_out), .D(Serial_Multiplicand), .Q(d_ff_2_q));  // open: Qn, preset, en, reset
  D_Flip_Flop d_ff_3 (.clk(CLK_out), .D(Serial_Multiplicand), .Q(d_ff_3_q));  // open: Qn, preset, en, reset
  D_Flip_Flop d_ff_4 (.clk(CLK_out), .D(Serial_Multiplicand), .Q(d_ff_4_q));  // open: Qn, preset, en, reset
  D_Flip_Flop d_ff_5 (.clk(CLK_out), .D(Serial_Multiplicand), .Q(d_ff_5_q));  // open: Qn, preset, en, reset
  D_Flip_Flop d_ff_6 (.clk(CLK_out), .D(Serial_Multiplicand), .Q(d_ff_6_q));  // open: Qn, preset, en, reset
  D_Flip_Flop d_ff_7 (.clk(CLK_out), .D(Serial_Multiplicand), .Q(d_ff_7_q));  // open: Qn, preset, en, reset
  and and_1 (and_1_out, Serial_Multiplier, Serial_Multiplicand);
  D_Flip_Flop d_ff_8 (.clk(CLK_out), .D(d_ff_1_q), .Q(d_ff_8_q));  // open: Qn, preset, en, reset
  D_Flip_Flop d_ff_9 (.clk(CLK_out), .D(d_ff_2_q), .Q(d_ff_9_q));  // open: Qn, preset, en, reset
  D_Flip_Flop d_ff_10 (.clk(CLK_out), .D(d_ff_3_q), .Q(d_ff_10_q));  // open: Qn, preset, en, reset
  D_Flip_Flop d_ff_11 (.clk(CLK_out), .D(d_ff_4_q), .Q(d_ff_11_q));  // open: Qn, preset, en, reset
  D_Flip_Flop d_ff_12 (.clk(CLK_out), .D(d_ff_5_q), .Q(d_ff_12_q));  // open: Qn, preset, en, reset
  D_Flip_Flop d_ff_13 (.clk(CLK_out), .D(d_ff_6_q), .Q(d_ff_13_q));  // open: Qn, preset, en, reset
  D_Flip_Flop d_ff_14 (.clk(CLK_out), .D(d_ff_7_q), .Q(d_ff_14_q));  // open: Qn, preset, en, reset
  D_Flip_Flop d_ff_15 (.clk(CLK_out), .D(and_1_out), .Q(d_ff_15_q));  // open: Qn, preset, en, reset
  D_Flip_Flop d_ff_16 (.clk(CLK_out), .D(d_ff_8_q), .Q(d_ff_16_q));  // open: Qn, preset, en, reset
  D_Flip_Flop d_ff_17 (.clk(CLK_out), .D(d_ff_9_q), .Q(d_ff_17_q));  // open: Qn, preset, en, reset
  D_Flip_Flop d_ff_18 (.clk(CLK_out), .D(d_ff_10_q), .Q(d_ff_18_q));  // open: Qn, preset, en, reset
  D_Flip_Flop d_ff_19 (.clk(CLK_out), .D(d_ff_11_q), .Q(d_ff_19_q));  // open: Qn, preset, en, reset
  D_Flip_Flop d_ff_20 (.clk(CLK_out), .D(d_ff_12_q), .Q(d_ff_20_q));  // open: Qn, preset, en, reset
  D_Flip_Flop d_ff_21 (.clk(CLK_out), .D(d_ff_13_q), .Q(d_ff_21_q));  // open: Qn, preset, en, reset
  and and_2 (and_2_out, Serial_Multiplier, d_ff_14_q);
  Adder #(.width(1)) adder_1 (.a(d_ff_15_q), .b(d_ff_22_q), .out(adder_1_out), .cin(and_2_out), .cout(adder_1_cout));
  D_Flip_Flop d_ff_22 (.clk(CLK_out), .D(adder_1_cout), .Q(d_ff_22_q));  // open: Qn, preset, en, reset
  D_Flip_Flop d_ff_23 (.clk(CLK_out), .D(d_ff_16_q), .Q(d_ff_23_q));  // open: Qn, preset, en, reset
  D_Flip_Flop d_ff_24 (.clk(CLK_out), .D(d_ff_17_q), .Q(d_ff_24_q));  // open: Qn, preset, en, reset
  D_Flip_Flop d_ff_25 (.clk(CLK_out), .D(d_ff_18_q), .Q(d_ff_25_q));  // open: Qn, preset, en, reset
  D_Flip_Flop d_ff_26 (.clk(CLK_out), .D(d_ff_19_q), .Q(d_ff_26_q));  // open: Qn, preset, en, reset
  D_Flip_Flop d_ff_27 (.clk(CLK_out), .D(d_ff_20_q), .Q(d_ff_27_q));  // open: Qn, preset, en, reset
  D_Flip_Flop d_ff_28 (.clk(CLK_out), .D(d_ff_21_q), .Q(d_ff_28_q));  // open: Qn, preset, en, reset
  and and_3 (and_3_out, Serial_Multiplier, d_ff_28_q);
  D_Flip_Flop d_ff_29 (.clk(CLK_out), .D(adder_1_out), .Q(d_ff_29_q));  // open: Qn, preset, en, reset
  D_Flip_Flop d_ff_30 (.clk(CLK_out), .D(d_ff_23_q), .Q(d_ff_30_q));  // open: Qn, preset, en, reset
  D_Flip_Flop d_ff_31 (.clk(CLK_out), .D(d_ff_24_q), .Q(d_ff_31_q));  // open: Qn, preset, en, reset
  D_Flip_Flop d_ff_32 (.clk(CLK_out), .D(d_ff_25_q), .Q(d_ff_32_q));  // open: Qn, preset, en, reset
  D_Flip_Flop d_ff_33 (.clk(CLK_out), .D(d_ff_26_q), .Q(d_ff_33_q));  // open: Qn, preset, en, reset
  D_Flip_Flop d_ff_34 (.clk(CLK_out), .D(d_ff_27_q), .Q(d_ff_34_q));  // open: Qn, preset, en, reset
  Adder #(.width(1)) adder_2 (.a(d_ff_29_q), .b(d_ff_35_q), .out(adder_2_out), .cin(and_3_out), .cout(adder_2_cout));
  D_Flip_Flop d_ff_35 (.clk(CLK_out), .D(adder_2_cout), .Q(d_ff_35_q));  // open: Qn, preset, en, reset
  D_Flip_Flop d_ff_36 (.clk(CLK_out), .D(d_ff_30_q), .Q(d_ff_36_q));  // open: Qn, preset, en, reset
  D_Flip_Flop d_ff_37 (.clk(CLK_out), .D(d_ff_31_q), .Q(d_ff_37_q));  // open: Qn, preset, en, reset
  D_Flip_Flop d_ff_38 (.clk(CLK_out), .D(d_ff_32_q), .Q(d_ff_38_q));  // open: Qn, preset, en, reset
  D_Flip_Flop d_ff_39 (.clk(CLK_out), .D(d_ff_33_q), .Q(d_ff_39_q));  // open: Qn, preset, en, reset
  D_Flip_Flop d_ff_40 (.clk(CLK_out), .D(d_ff_34_q), .Q(d_ff_40_q));  // open: Qn, preset, en, reset
  and and_4 (and_4_out, Serial_Multiplier, d_ff_40_q);
  D_Flip_Flop d_ff_41 (.clk(CLK_out), .D(adder_2_out), .Q(d_ff_41_q));  // open: Qn, preset, en, reset
  Adder #(.width(1)) adder_3 (.a(d_ff_41_q), .b(d_ff_42_q), .out(adder_3_out), .cin(and_4_out), .cout(adder_3_cout));
  D_Flip_Flop d_ff_42 (.clk(CLK_out), .D(adder_3_cout), .Q(d_ff_42_q));  // open: Qn, preset, en, reset
  D_Flip_Flop d_ff_43 (.clk(CLK_out), .D(d_ff_36_q), .Q(d_ff_43_q));  // open: Qn, preset, en, reset
  D_Flip_Flop d_ff_44 (.clk(CLK_out), .D(d_ff_37_q), .Q(d_ff_44_q));  // open: Qn, preset, en, reset
  D_Flip_Flop d_ff_45 (.clk(CLK_out), .D(d_ff_38_q), .Q(d_ff_45_q));  // open: Qn, preset, en, reset
  D_Flip_Flop d_ff_46 (.clk(CLK_out), .D(d_ff_39_q), .Q(d_ff_46_q));  // open: Qn, preset, en, reset
  and and_5 (and_5_out, Serial_Multiplier, d_ff_52_q);
  D_Flip_Flop d_ff_47 (.clk(CLK_out), .D(adder_3_out), .Q(d_ff_47_q));  // open: Qn, preset, en, reset
  Adder #(.width(1)) adder_4 (.a(d_ff_47_q), .b(d_ff_48_q), .out(adder_4_out), .cin(and_5_out), .cout(adder_4_cout));
  D_Flip_Flop d_ff_48 (.clk(CLK_out), .D(adder_4_cout), .Q(d_ff_48_q));  // open: Qn, preset, en, reset
  D_Flip_Flop d_ff_49 (.clk(CLK_out), .D(d_ff_43_q), .Q(d_ff_49_q));  // open: Qn, preset, en, reset
  D_Flip_Flop d_ff_50 (.clk(CLK_out), .D(d_ff_44_q), .Q(d_ff_50_q));  // open: Qn, preset, en, reset
  D_Flip_Flop d_ff_51 (.clk(CLK_out), .D(d_ff_45_q), .Q(d_ff_51_q));  // open: Qn, preset, en, reset
  D_Flip_Flop d_ff_52 (.clk(CLK_out), .D(d_ff_46_q), .Q(d_ff_52_q));  // open: Qn, preset, en, reset
  D_Flip_Flop d_ff_53 (.clk(CLK_out), .D(adder_4_out), .Q(d_ff_53_q));  // open: Qn, preset, en, reset
  D_Flip_Flop d_ff_54 (.clk(CLK_out), .D(d_ff_49_q), .Q(d_ff_54_q));  // open: Qn, preset, en, reset
  D_Flip_Flop d_ff_55 (.clk(CLK_out), .D(d_ff_50_q), .Q(d_ff_55_q));  // open: Qn, preset, en, reset
  D_Flip_Flop d_ff_56 (.clk(CLK_out), .D(d_ff_51_q), .Q(d_ff_56_q));  // open: Qn, preset, en, reset
  and and_6 (and_6_out, Serial_Multiplier, d_ff_60_q);
  Adder #(.width(1)) adder_5 (.a(d_ff_53_q), .b(d_ff_57_q), .out(adder_5_out), .cin(and_6_out), .cout(adder_5_cout));
  D_Flip_Flop d_ff_57 (.clk(CLK_out), .D(adder_5_cout), .Q(d_ff_57_q));  // open: Qn, preset, en, reset
  D_Flip_Flop d_ff_58 (.clk(CLK_out), .D(d_ff_54_q), .Q(d_ff_58_q));  // open: Qn, preset, en, reset
  D_Flip_Flop d_ff_59 (.clk(CLK_out), .D(d_ff_55_q), .Q(d_ff_59_q));  // open: Qn, preset, en, reset
  D_Flip_Flop d_ff_60 (.clk(CLK_out), .D(d_ff_56_q), .Q(d_ff_60_q));  // open: Qn, preset, en, reset
  D_Flip_Flop d_ff_61 (.clk(CLK_out), .D(adder_5_out), .Q(d_ff_61_q));  // open: Qn, preset, en, reset
  D_Flip_Flop d_ff_62 (.clk(CLK_out), .D(d_ff_58_q), .Q(d_ff_62_q));  // open: Qn, preset, en, reset
  D_Flip_Flop d_ff_63 (.clk(CLK_out), .D(d_ff_59_q), .Q(d_ff_63_q));  // open: Qn, preset, en, reset
  and and_7 (and_7_out, Serial_Multiplier, d_ff_66_q);
  Adder #(.width(1)) adder_6 (.a(d_ff_61_q), .b(d_ff_64_q), .out(adder_6_out), .cin(and_7_out), .cout(adder_6_cout));
  D_Flip_Flop d_ff_64 (.clk(CLK_out), .D(adder_6_cout), .Q(d_ff_64_q));  // open: Qn, preset, en, reset
  D_Flip_Flop d_ff_65 (.clk(CLK_out), .D(d_ff_62_q), .Q(d_ff_65_q));  // open: Qn, preset, en, reset
  D_Flip_Flop d_ff_66 (.clk(CLK_out), .D(d_ff_63_q), .Q(d_ff_66_q));  // open: Qn, preset, en, reset
  D_Flip_Flop d_ff_67 (.clk(CLK_out), .D(adder_6_out), .Q(d_ff_67_q));  // open: Qn, preset, en, reset
  and and_8 (and_8_out, Serial_Multiplier, d_ff_71_q);
  Adder #(.width(1)) adder_7 (.a(d_ff_67_q), .b(d_ff_68_q), .out(adder_7_out), .cin(and_8_out), .cout(adder_7_cout));
  D_Flip_Flop d_ff_68 (.clk(CLK_out), .D(adder_7_cout), .Q(d_ff_68_q));  // open: Qn, preset, en, reset
  D_Flip_Flop d_ff_69 (.clk(CLK_out), .D(d_ff_65_q), .Q(d_ff_69_q));  // open: Qn, preset, en, reset
  D_Flip_Flop d_ff_70 (.clk(CLK_out), .D(adder_7_out), .Q(d_ff_70_q));  // open: Qn, preset, en, reset
  D_Flip_Flop d_ff_71 (.clk(CLK_out), .D(d_ff_69_q), .Q(d_ff_71_q));  // open: Qn, preset, en, reset
  Shift_Register #(.length(16)) shift_register_1 (
    .in(d_ff_70_q), .clk(CLK_out));  // open: shift, out, load, clr, d0, q0, d1, q1, d2, q2, d3, q3, d4, q4, d5, q5, d6, q6, d7, q7, d8, q8, d9, q9, d10, q10, d11, q11, d12, q12, d13, q13, d14, q14, d15, q15
endmodule
