// Logisim project serialY_parallelX_multiplier_8bit.circ as structural Verilog: 1 circuit, main circuit main
module main (
  input  in_1,
  input  in_2,
  input  in_3,
  input  in_4,
  input  in_5,
  input  in_6,
  input  in_7,
  input  in_8,
  input  Serial_Multiplier
);

  wire adder_1_cout, adder_1_out, adder_2_cout, adder_2_out, adder_3_cout, adder_3_out, adder_4_cout,
       adder_4_out, adder_5_cout, adder_5_out, adder_6_cout, adder_6_out, adder_7_cout, adder_7_out,
       and_1_out, and_2_out, and_3_out, and_4_out, and_5_out, and_6_out, and_7_out, and_8_out, CLK_out,
       d_ff_1_q, d_ff_2_q, d_ff_3_q, d_ff_4_q, d_ff_5_q, d_ff_6_q, d_ff_7_q, d_ff_8_q, d_ff_9_q, d_ff_10_q,
       d_ff_11_q, d_ff_12_q, d_ff_13_q, d_ff_14_q, d_ff_15_q;

  Clock CLK (.out(CLK_out));
  and and_1 (and_1_out, Serial_Multiplier, in_1);
  D_Flip_Flop d_ff_1 (.clk(CLK_out), .D(and_1_out), .Q(d_ff_1_q));  // open: Qn, preset, en, reset
  and and_2 (and_2_out, Serial_Multiplier, in_2);
  Adder #(.width(1)) adder_1 (.a(d_ff_1_q), .b(d_ff_2_q), .out(adder_1_out), .cin(and_2_out), .cout(adder_1_cout));
  D_Flip_Flop d_ff_2 (.clk(CLK_out), .D(adder_1_cout), .Q(d_ff_2_q));  // open: Qn, preset, en, reset
  D_Flip_Flop d_ff_3 (.clk(CLK_out), .D(adder_1_out), .Q(d_ff_3_q));  // open: Qn, preset, en, reset
  and and_3 (and_3_out, Serial_Multiplier, in_3);
  Adder #(.width(1)) adder_2 (.a(d_ff_3_q), .b(d_ff_4_q), .out(adder_2_out), .cin(and_3_out), .cout(adder_2_cout));
  D_Flip_Flop d_ff_4 (.clk(CLK_out), .D(adder_2_cout), .Q(d_ff_4_q));  // open: Qn, preset, en, reset
  D_Flip_Flop d_ff_5 (.clk(CLK_out), .D(adder_2_out), .Q(d_ff_5_q));  // open: Qn, preset, en, reset
  and and_4 (and_4_out, Serial_Multiplier, in_4);
  Adder #(.width(1)) adder_3 (.a(d_ff_5_q), .b(d_ff_6_q), .out(adder_3_out), .cin(and_4_out), .cout(adder_3_cout));
  D_Flip_Flop d_ff_6 (.clk(CLK_out), .D(adder_3_cout), .Q(d_ff_6_q));  // open: Qn, preset, en, reset
  and and_5 (and_5_out, Serial_Multiplier, in_5);
  D_Flip_Flop d_ff_7 (.clk(CLK_out), .D(adder_3_out), .Q(d_ff_7_q));  // open: Qn, preset, en, reset
  Adder #(.width(1)) adder_4 (.a(d_ff_7_q), .b(d_ff_8_q), .out(adder_4_out), .cin(and_5_out), .cout(adder_4_cout));
  D_Flip_Flop d_ff_8 (.clk(CLK_out), .D(adder_4_cout), .Q(d_ff_8_q));  // open: Qn, preset, en, reset
  and and_6 (and_6_out, Serial_Multiplier, in_6);
  D_Flip_Flop d_ff_9 (.clk(CLK_out), .D(adder_4_out), .Q(d_ff_9_q));  // open: Qn, preset, en, reset
  Adder #(.width(1)) adder_5 (.a(d_ff_9_q), .b(d_ff_10_q), .out(adder_5_out), .cin(and_6_out), .cout(adder_5_cout));
  D_Flip_Flop d_ff_10 (.clk(CLK_out), .D(adder_5_cout), .Q(d_ff_10_q));  // open: Qn, preset, en, reset
  and and_7 (and_7_out, Serial_Multiplier, in_7);
  D_Flip_Flop d_ff_11 (.clk(CLK_out), .D(adder_5_out), .Q(d_ff_11_q));  // open: Qn, preset, en, reset
  Adder #(.width(1)) adder_6 (.a(d_ff_11_q), .b(d_ff_12_q), .out(adder_6_out), .cin(and_7_out), .cout(adder_6_cout));
  D_Flip_Flop d_ff_12 (.clk(CLK_out), .D(adder_6_cout), .Q(d_ff_12_q));  // open: Qn, preset, en, reset
  D_Flip_Flop d_ff_13 (.clk(CLK_out), .D(adder_6_out), .Q(d_ff_13_q));  // open: Qn, preset, en, reset
  and and_8 (and_8_out, Serial_Multiplier, in_8);
  Adder #(.width(1)) adder_7 (.a(d_ff_13_q), .b(d_ff_14_q), .out(adder_7_out), .cin(and_8_out), .cout(adder_7_cout));
  D_Flip_Flop d_ff_14 (.clk(CLK_out), .D(adder_7_cout), .Q(d_ff_14_q));  // open: Qn, preset, en, reset
  D_Flip_Flop d_ff_15 (.clk(CLK_out), .D(adder_7_out), .Q(d_ff_15_q));  // open: Qn, preset, en, reset
  Shift_Register #(.length(16)) shift_register_1 (
    .in(d_ff_15_q), .clk(CLK_out));  // open: shift, out, load, clr, d0, q0, d1, q1, d2, q2, d3, q3, d4, q4, d5, q5, d6, q6, d7, q7, d8, q8, d9, q9, d10, q10, d11, q11, d12, q12, d13, q13, d14, q14, d15, q15
endmodule
