// Logisim project multiplier.circ as structural Verilog: 1 circuit, main circuit main
module main (
  input  in_1,
  input  in_2,
  input  in_3,
  input  in_4,
  input  Load,
  input  in_6,
  input  in_7,
  input  in_8,
  input  in_9,
  input  in_10,
  input  in_11,
  input  in_12,
  input  in_13,
  input  in_14,
  input  Shift,
  input  in_16,
  input  [7:0] in_17,
  input  [7:0] in_18,
  input  in_19,
  input  in_20,
  output out_21,
  output out_22,
  output out_23,
  output out_24,
  output out_25,
  output out_26,
  output out_27,
  output out_28
);

  wire adder_2_cout, adder_2_out, adder_3_cout, adder_4_cout, adder_4_out, adder_5_cout, adder_5_out,
       adder_6_cout, adder_7_cout, adder_7_out, adder_8_cout, adder_8_out, adder_9_cout, adder_9_out,
       adder_10_cout, adder_11_cout, adder_11_out, adder_12_cout, adder_12_out, adder_13_cout, adder_13_out,
       adder_14_cout, adder_15_cout, adder_15_out, adder_16_cout, adder_16_out, adder_17_cout, adder_18_cout,
       adder_18_out, adder_19_cout, adder_20_cout, adder_21_cout, and_1_out, and_2_out, and_3_out, and_4_out,
       and_5_out, and_6_out, and_7_out, and_8_out, and_9_out, and_10_out, and_11_out, and_12_out, and_13_out,
       and_14_out, and_15_out, and_16_out, Carry_q, clock_1_out, shift_register_1_out, shift_register_2_out;
  wire [7:0] adder_21_out, multiplexer_1_out, shift_register_1_q7;

  Adder #(.width(1)) adder_1 (.a(adder_2_cout), .b(1'b0), .out(out_21), .cin(adder_3_cout));  // open: cout
  and and_1 (and_1_out, in_20, in_1);
  Adder #(.width(1)) adder_2 (.a(1'b0), .b(and_1_out), .out(adder_2_out), .cin(adder_4_cout), .cout(adder_2_cout));
  Adder #(.width(1)) adder_3 (.a(adder_5_cout), .b(adder_2_out), .out(out_22), .cin(adder_6_cout), .cout(adder_3_cout));
  and and_2 (and_2_out, in_19, in_1);
  and and_3 (and_3_out, in_20, in_2);
  Adder #(.width(1)) adder_4 (.a(1'b0), .b(and_2_out), .out(adder_4_out), .cin(adder_7_cout), .cout(adder_4_cout));
  Adder #(.width(1)) adder_5 (
    .a(adder_4_out), .b(and_3_out), .out(adder_5_out), .cin(adder_8_cout), .cout(adder_5_cout));
  Adder #(.width(1)) adder_6 (
    .a(adder_9_cout), .b(adder_5_out), .out(out_23), .cin(adder_10_cout), .cout(adder_6_cout));
  and and_4 (and_4_out, in_16, in_1);
  Adder #(.width(1)) adder_7 (.a(1'b0), .b(and_4_out), .out(adder_7_out), .cin(adder_11_cout), .cout(adder_7_cout));
  and and_5 (and_5_out, in_19, in_2);
  Adder #(.width(1)) adder_8 (
    .a(adder_7_out), .b(and_5_out), .out(adder_8_out), .cin(adder_12_cout), .cout(adder_8_cout));
  and and_6 (and_6_out, in_20, in_3);
  Adder #(.width(1)) adder_9 (
    .a(adder_8_out), .b(and_6_out), .out(adder_9_out), .cin(adder_13_cout), .cout(adder_9_cout));
  Adder #(.width(1)) adder_10 (.a(adder_14_cout), .b(adder_9_out), .out(out_24), .cin(1'b0), .cout(adder_10_cout));
  and and_7 (and_7_out, in_14, in_1);
  and and_8 (and_8_out, in_16, in_2);
  and and_9 (and_9_out, in_19, in_3);
  and and_10 (and_10_out, in_20, in_4);
  Adder #(.width(1)) adder_11 (.a(1'b0), .b(and_7_out), .out(adder_11_out), .cin(1'b0), .cout(adder_11_cout));
  Adder #(.width(1)) adder_12 (
    .a(adder_11_out), .b(and_8_out), .out(adder_12_out), .cin(adder_15_cout), .cout(adder_12_cout));
  Adder #(.width(1)) adder_13 (
    .a(adder_12_out), .b(and_9_out), .out(adder_13_out), .cin(adder_16_cout), .cout(adder_13_cout));
  Adder #(.width(1)) adder_14 (
    .a(adder_13_out), .b(and_10_out), .out(out_25), .cin(adder_17_cout), .cout(adder_14_cout));
  and and_11 (and_11_out, in_14, in_2);
  Adder #(.width(1)) adder_15 (.a(1'b0), .b(and_11_out), .out(adder_15_out), .cin(1'b0), .cout(adder_15_cout));
  and and_12 (and_12_out, in_16, in_3);
  Adder #(.width(1)) adder_16 (
    .a(adder_15_out), .b(and_12_out), .out(adder_16_out), .cin(adder_18_cout), .cout(adder_16_cout));
  and and_13 (and_13_out, in_19, in_4);
  Adder #(.width(1)) adder_17 (
    .a(adder_16_out), .b(and_13_out), .out(out_26), .cin(adder_19_cout), .cout(adder_17_cout));
  and and_14 (and_14_out, in_14, in_3);
  and and_15 (and_15_out, in_16, in_4);
  Adder #(.width(1)) adder_18 (.a(1'b0), .b(and_14_out), .out(adder_18_out), .cin(1'b0), .cout(adder_18_cout));
  Adder #(.width(1)) adder_19 (
    .a(adder_18_out), .b(and_15_out), .out(out_27), .cin(adder_20_cout), .cout(adder_19_cout));
  and and_16 (and_16_out, in_14, in_4);
  Adder #(.width(1)) adder_20 (.a(1'b0), .b(and_16_out), .out(out_28), .cin(1'b0), .cout(adder_20_cout));
  D_Flip_Flop Carry (.D(adder_21_cout), .Q(Carry_q));  // open: clk, Qn, preset, en, reset
  Clock clock_1 (.out(clock_1_out));
  Shift_Register shift_register_1 (
    .shift(Shift), .in(Carry_q), .clk(clock_1_out), .out(shift_register_1_out), .d0(adder_21_out[7]),
    .q0(shift_register_1_q7[7]), .d1(adder_21_out[6]), .q1(shift_register_1_q7[6]), .d2(adder_21_out[5]),
    .q2(shift_register_1_q7[5]), .d3(adder_21_out[4]), .q3(shift_register_1_q7[4]), .d4(adder_21_out[3]),
    .q4(shift_register_1_q7[3]), .d5(adder_21_out[2]), .q5(shift_register_1_q7[2]), .d6(adder_21_out[1]),
    .q6(shift_register_1_q7[1]), .d7(adder_21_out[0]), .q7(shift_register_1_q7[0]));  // open: load, clr
  Adder adder_21 (.a(multiplexer_1_out), .b(shift_register_1_q7), .out(adder_21_out), .cin(1'b0), .cout(adder_21_cout));
  Shift_Register shift_register_2 (
    .shift(Shift), .in(shift_register_1_out), .clk(clock_1_out), .out(shift_register_2_out), .load(Load),
    .d0(in_6), .d1(in_7), .d2(in_8), .d3(in_9), .d4(in_10), .d5(in_11), .d6(in_12), .d7(in_13));  // open: clr, q0, q1, q2, q3, q4, q5, q6, q7
  Multiplexer #(.width(8)) multiplexer_1 (
    .in0(in_17), .in1(in_18), .out(multiplexer_1_out), .sel(shift_register_2_out));  // open: en
  Adder adder_22 ();  // open: a, b, out, cin, cout

  // Notes on the sheet:
  //   Enter values to be multiplied (Multiplier)
endmodule
