// Logisim project registers.circ as structural Verilog: 1 circuit, main circuit main
module main (
  input  in_1,
  input  in_2,
  input  in_3,
  input  in_4,
  input  in_5,
  input  in_6,
  input  in_7,
  input  in_8,
  input  in_9,
  input  in_10,
  input  in_11,
  input  in_12,
  input  in_13,
  input  in_14,
  input  in_15,
  input  in_16,
  input  in_17,
  output out_18
);

  wire clock_1_out, clock_2_out, d_ff_1_q, d_ff_2_q, d_ff_3_q, d_ff_4_q, d_ff_5_q, d_ff_6_q, d_ff_7_q,
       d_ff_8_q, d_ff_9_q, d_ff_10_q, d_ff_11_q, d_ff_12_q, d_ff_13_q, d_ff_14_q, d_ff_16_q, d_ff_17_q,
       d_ff_18_q, d_ff_19_q, d_ff_20_q, d_ff_21_q, d_ff_22_q, d_ff_23_q, d_ff_24_q, multiplexer_1_out,
       multiplexer_2_out, multiplexer_3_out, multiplexer_4_out, multiplexer_5_out, multiplexer_6_out,
       multiplexer_7_out, multiplexer_8_out, multiplexer_9_out, multiplexer_10_out, multiplexer_11_out,
       multiplexer_12_out, multiplexer_13_out, multiplexer_14_out, multiplexer_15_out, multiplexer_16_out,
       undriven;

  Clock clock_1 (.out(clock_1_out));
  Clock clock_2 (.out(clock_2_out));
  D_Flip_Flop d_ff_1 (.clk(clock_1_out), .D(undriven), .Q(d_ff_1_q));  // open: Qn, preset, en, reset
  Multiplexer multiplexer_1 (.in0(d_ff_2_q), .in1(in_1), .out(multiplexer_1_out), .sel(in_17));  // open: en
  D_Flip_Flop d_ff_2 (.clk(clock_2_out), .Q(d_ff_2_q));  // open: D, Qn, preset, en, reset
  D_Flip_Flop d_ff_3 (.clk(clock_1_out), .D(d_ff_1_q), .Q(d_ff_3_q));  // open: Qn, preset, en, reset
  Multiplexer multiplexer_2 (.in0(d_ff_4_q), .in1(in_2), .out(multiplexer_2_out), .sel(in_17));  // open: en
  D_Flip_Flop d_ff_4 (.clk(clock_2_out), .D(multiplexer_1_out), .Q(d_ff_4_q));  // open: Qn, preset, en, reset
  D_Flip_Flop d_ff_5 (.clk(clock_1_out), .D(d_ff_3_q), .Q(d_ff_5_q));  // open: Qn, preset, en, reset
  Multiplexer multiplexer_3 (.in0(d_ff_6_q), .in1(in_3), .out(multiplexer_3_out), .sel(in_17));  // open: en
  D_Flip_Flop d_ff_6 (.clk(clock_2_out), .D(multiplexer_2_out), .Q(d_ff_6_q));  // open: Qn, preset, en, reset
  D_Flip_Flop d_ff_7 (.clk(clock_1_out), .D(d_ff_5_q), .Q(d_ff_7_q));  // open: Qn, preset, en, reset
  D_Flip_Flop d_ff_8 (.clk(clock_2_out), .D(multiplexer_3_out), .Q(d_ff_8_q));  // open: Qn, preset, en, reset
  Multiplexer multiplexer_4 (.in0(d_ff_8_q), .in1(in_4), .out(multiplexer_4_out), .sel(in_17));  // open: en
  D_Flip_Flop d_ff_9 (.clk(clock_1_out), .D(d_ff_7_q), .Q(d_ff_9_q));  // open: Qn, preset, en, reset
  Multiplexer multiplexer_5 (.in0(d_ff_10_q), .in1(in_5), .out(multiplexer_5_out), .sel(in_17));  // open: en
  D_Flip_Flop d_ff_10 (.clk(clock_2_out), .D(multiplexer_4_out), .Q(d_ff_10_q));  // open: Qn, preset, en, reset
  D_Flip_Flop d_ff_11 (.clk(clock_1_out), .D(d_ff_9_q), .Q(d_ff_11_q));  // open: Qn, preset, en, reset
  Multiplexer multiplexer_6 (.in0(d_ff_12_q), .in1(in_6), .out(multiplexer_6_out), .sel(in_17));  // open: en
  D_Flip_Flop d_ff_12 (.clk(clock_2_out), .D(multiplexer_5_out), .Q(d_ff_12_q));  // open: Qn, preset, en, reset
  D_Flip_Flop d_ff_13 (.clk(clock_1_out), .D(d_ff_11_q), .Q(d_ff_13_q));  // open: Qn, preset, en, reset
  D_Flip_Flop d_ff_14 (.clk(clock_2_out), .D(multiplexer_6_out), .Q(d_ff_14_q));  // open: Qn, preset, en, reset
  Multiplexer multiplexer_7 (.in0(d_ff_14_q), .in1(in_7), .out(multiplexer_7_out), .sel(in_17));  // open: en
  D_Flip_Flop d_ff_15 (.clk(clock_1_out), .D(d_ff_13_q));  // open: Q, Qn, preset, en, reset
  Multiplexer multiplexer_8 (.in0(d_ff_16_q), .in1(in_8), .out(multiplexer_8_out), .sel(in_17));  // open: en
  D_Flip_Flop d_ff_16 (.clk(clock_2_out), .D(multiplexer_7_out), .Q(d_ff_16_q));  // open: Qn, preset, en, reset
  Multiplexer multiplexer_9 (.in0(d_ff_17_q), .in1(in_9), .out(multiplexer_9_out), .sel(in_17));  // open: en
  D_Flip_Flop d_ff_17 (.clk(clock_2_out), .D(multiplexer_8_out), .Q(d_ff_17_q));  // open: Qn, preset, en, reset
  D_Flip_Flop d_ff_18 (.clk(clock_2_out), .D(multiplexer_9_out), .Q(d_ff_18_q));  // open: Qn, preset, en, reset
  Multiplexer multiplexer_10 (.in0(d_ff_18_q), .in1(in_10), .out(multiplexer_10_out), .sel(in_17));  // open: en
  D_Flip_Flop d_ff_19 (.clk(clock_2_out), .D(multiplexer_10_out), .Q(d_ff_19_q));  // open: Qn, preset, en, reset
  Multiplexer multiplexer_11 (.in0(d_ff_19_q), .in1(in_11), .out(multiplexer_11_out), .sel(in_17));  // open: en
  Multiplexer multiplexer_12 (.in0(d_ff_20_q), .in1(in_12), .out(multiplexer_12_out), .sel(in_17));  // open: en
  D_Flip_Flop d_ff_20 (.clk(clock_2_out), .D(multiplexer_11_out), .Q(d_ff_20_q));  // open: Qn, preset, en, reset
  D_Flip_Flop d_ff_21 (.clk(clock_2_out), .D(multiplexer_12_out), .Q(d_ff_21_q));  // open: Qn, preset, en, reset
  Multiplexer multiplexer_13 (.in0(d_ff_21_q), .in1(in_13), .out(multiplexer_13_out), .sel(in_17));  // open: en
  Multiplexer multiplexer_14 (.in0(d_ff_22_q), .in1(in_14), .out(multiplexer_14_out), .sel(in_17));  // open: en
  D_Flip_Flop d_ff_22 (.clk(clock_2_out), .D(multiplexer_13_out), .Q(d_ff_22_q));  // open: Qn, preset, en, reset
  Multiplexer multiplexer_15 (.in0(d_ff_23_q), .in1(in_15), .out(multiplexer_15_out), .sel(in_17));  // open: en
  D_Flip_Flop d_ff_23 (.clk(clock_2_out), .D(multiplexer_14_out), .Q(d_ff_23_q));  // open: Qn, preset, en, reset
  Multiplexer multiplexer_16 (.in0(d_ff_24_q), .in1(in_16), .out(multiplexer_16_out), .sel(in_17));  // open: en
  D_Flip_Flop d_ff_24 (.clk(clock_2_out), .D(multiplexer_15_out), .Q(d_ff_24_q));  // open: Qn, preset, en, reset
  D_Flip_Flop d_ff_25 (.clk(clock_2_out), .D(multiplexer_16_out), .Q(out_18));  // open: Qn, preset, en, reset
endmodule
