// Logisim project serial multiplier.circ as structural Verilog: 1 circuit, main circuit main
module main (
  input  Serial_Multiplicand,
  input  Serial_Multiplier,
  output out_3,
  output out_4,
  output out_5,
  output out_6,
  output out_7,
  output out_8,
  output out_9,
  output out_10
);

  wire adder_2_cout, adder_2_out, adder_3_cout, adder_4_cout, adder_4_out, adder_5_cout, adder_5_out,
       adder_6_cout, adder_7_cout, adder_7_out, adder_8_cout, adder_8_out, adder_9_cout, adder_9_out,
       adder_10_cout, adder_11_cout, adder_11_out, adder_12_cout, adder_12_out, adder_13_cout, adder_13_out,
       adder_14_cout, adder_15_cout, adder_15_out, adder_16_cout, adder_16_out, adder_17_cout, adder_18_cout,
       adder_18_out, adder_19_cout, adder_20_cout, and_1_out, and_2_out, and_3_out, and_4_out, and_5_out,
       and_6_out, and_7_out, and_8_out, and_9_out, and_10_out, and_11_out, and_12_out, and_13_out,
       and_14_out, and_15_out, and_16_out, clock_1_out, shift_register_1_q0, shift_register_1_q1,
       shift_register_1_q2, shift_register_1_q3, shift_register_2_q0, shift_register_2_q1,
       shift_register_2_q2, shift_register_2_q3;

  Clock clock_1 (.out(clock_1_out));
  Shift_Register #(.length(4)) shift_register_1 (
    .shift(1'b1), .in(Serial_Multiplier), .clk(clock_1_out), .q0(shift_register_1_q0),
    .q1(shift_register_1_q1), .q2(shift_register_1_q2), .q3(shift_register_1_q3));  // open: out, load, clr, d0, d1, d2, d3
  Adder #(.width(1)) adder_1 (.a(adder_2_cout), .b(1'b0), .out(out_3), .cin(adder_3_cout));  // open: cout
  and and_1 (and_1_out, shift_register_1_q0, shift_register_2_q0);
  Adder #(.width(1)) adder_2 (.a(1'b0), .b(and_1_out), .out(adder_2_out), .cin(adder_4_cout), .cout(adder_2_cout));
  Adder #(.width(1)) adder_3 (.a(adder_5_cout), .b(adder_2_out), .out(out_4), .cin(adder_6_cout), .cout(adder_3_cout));
  and and_2 (and_2_out, shift_register_1_q1, shift_register_2_q0);
  Adder #(.width(1)) adder_4 (.a(1'b0), .b(and_2_out), .out(adder_4_out), .cin(adder_7_cout), .cout(adder_4_cout));
  and and_3 (and_3_out, shift_register_1_q0, shift_register_2_q1);
  Adder #(.width(1)) adder_5 (
    .a(adder_4_out), .b(and_3_out), .out(adder_5_out), .cin(adder_8_cout), .cout(adder_5_cout));
  Adder #(.width(1)) adder_6 (.a(adder_9_cout), .b(adder_5_out), .out(out_5), .cin(adder_10_cout), .cout(adder_6_cout));
  and and_4 (and_4_out, shift_register_1_q2, shift_register_2_q0);
  and and_5 (and_5_out, shift_register_1_q1, shift_register_2_q1);
  and and_6 (and_6_out, shift_register_1_q0, shift_register_2_q2);
  Adder #(.width(1)) adder_7 (.a(1'b0), .b(and_4_out), .out(adder_7_out), .cin(adder_11_cout), .cout(adder_7_cout));
  Adder #(.width(1)) adder_8 (
    .a(adder_7_out), .b(and_5_out), .out(adder_8_out), .cin(adder_12_cout), .cout(adder_8_cout));
  Adder #(.width(1)) adder_9 (
    .a(adder_8_out), .b(and_6_out), .out(adder_9_out), .cin(adder_13_cout), .cout(adder_9_cout));
  Adder #(.width(1)) adder_10 (.a(adder_14_cout), .b(adder_9_out), .out(out_6), .cin(1'b0), .cout(adder_10_cout));
  and and_7 (and_7_out, shift_register_1_q3, shift_register_2_q0);
  Adder #(.width(1)) adder_11 (.a(1'b0), .b(and_7_out), .out(adder_11_out), .cin(1'b0), .cout(adder_11_cout));
  and and_8 (and_8_out, shift_register_1_q2, shift_register_2_q1);
  Adder #(.width(1)) adder_12 (
    .a(adder_11_out), .b(and_8_out), .out(adder_12_out), .cin(adder_15_cout), .cout(adder_12_cout));
  and and_9 (and_9_out, shift_register_1_q1, shift_register_2_q2);
  Adder #(.width(1)) adder_13 (
    .a(adder_12_out), .b(and_9_out), .out(adder_13_out), .cin(adder_16_cout), .cout(adder_13_cout));
  and and_10 (and_10_out, shift_register_1_q0, shift_register_2_q3);
  Adder #(.width(1)) adder_14 (
    .a(adder_13_out), .b(and_10_out), .out(out_7), .cin(adder_17_cout), .cout(adder_14_cout));
  and and_11 (and_11_out, shift_register_1_q3, shift_register_2_q1);
  and and_12 (and_12_out, shift_register_1_q2, shift_register_2_q2);
  and and_13 (and_13_out, shift_register_1_q1, shift_register_2_q3);
  Shift_Register #(.length(4)) shift_register_2 (
    .shift(1'b1), .in(Serial_Multiplicand), .clk(clock_1_out), .q0(shift_register_2_q0),
    .q1(shift_register_2_q1), .q2(shift_register_2_q2), .q3(shift_register_2_q3));  // open: out, load, clr, d0, d1, d2, d3
  Adder #(.width(1)) adder_15 (.a(1'b0), .b(and_11_out), .out(adder_15_out), .cin(1'b0), .cout(adder_15_cout));
  Adder #(.width(1)) adder_16 (
    .a(adder_15_out), .b(and_12_out), .out(adder_16_out), .cin(adder_18_cout), .cout(adder_16_cout));
  Adder #(.width(1)) adder_17 (
    .a(adder_16_out), .b(and_13_out), .out(out_8), .cin(adder_19_cout), .cout(adder_17_cout));
  and and_14 (and_14_out, shift_register_1_q3, shift_register_2_q2);
  Adder #(.width(1)) adder_18 (.a(1'b0), .b(and_14_out), .out(adder_18_out), .cin(1'b0), .cout(adder_18_cout));
  and and_15 (and_15_out, shift_register_1_q2, shift_register_2_q3);
  Adder #(.width(1)) adder_19 (
    .a(adder_18_out), .b(and_15_out), .out(out_9), .cin(adder_20_cout), .cout(adder_19_cout));
  and and_16 (and_16_out, shift_register_1_q3, shift_register_2_q3);
  Adder #(.width(1)) adder_20 (.a(1'b0), .b(and_16_out), .out(out_10), .cin(1'b0), .cout(adder_20_cout));
endmodule
