// Logisim project serial_multiplier_8bit.circ as structural Verilog: 1 circuit, main circuit main
module main (
  input  Serial_Multiplicand,
  input  Serial_Multiplier,
  input  Clear,
  output out_4
);

  wire adder_1_out, adder_2_cout, adder_2_out, adder_3_cout, adder_3_out, adder_4_cout, adder_4_out,
       adder_5_cout, adder_5_out, adder_6_cout, adder_6_out, adder_7_cout, adder_7_out, adder_8_cout,
       adder_8_out, adder_9_cout, adder_9_out, adder_10_cout, adder_10_out, adder_11_cout, adder_11_out,
       adder_12_cout, adder_12_out, adder_13_cout, adder_13_out, adder_14_cout, adder_14_out, adder_15_cout,
       adder_15_out, adder_16_cout, adder_16_out, adder_17_cout, adder_17_out, adder_18_cout, adder_18_out,
       adder_19_cout, adder_19_out, adder_20_cout, adder_20_out, adder_21_cout, adder_21_out, adder_22_cout,
       adder_22_out, adder_23_cout, adder_23_out, adder_24_cout, adder_24_out, adder_25_cout, adder_25_out,
       adder_26_cout, adder_26_out, adder_27_cout, adder_27_out, adder_28_cout, adder_28_out, adder_29_cout,
       adder_29_out, adder_30_cout, adder_30_out, adder_31_cout, adder_31_out, adder_32_cout, adder_32_out,
       adder_33_cout, adder_33_out, adder_34_cout, adder_34_out, adder_35_cout, adder_35_out, adder_36_cout,
       adder_36_out, adder_37_cout, adder_37_out, adder_38_cout, adder_38_out, adder_39_cout, adder_39_out,
       adder_40_cout, adder_40_out, adder_41_cout, adder_41_out, adder_42_cout, adder_42_out, adder_43_cout,
       adder_43_out, adder_44_cout, adder_44_out, adder_45_cout, adder_45_out, adder_46_cout, adder_46_out,
       adder_47_cout, adder_47_out, adder_48_cout, adder_48_out, adder_49_cout, adder_49_out, adder_50_cout,
       adder_50_out, adder_51_cout, adder_51_out, adder_52_cout, adder_52_out, adder_53_cout, adder_53_out,
       adder_54_cout, adder_54_out, adder_55_cout, adder_55_out, adder_56_cout, adder_56_out, adder_57_cout,
       adder_57_out, adder_58_cout, adder_58_out, adder_59_cout, adder_59_out, adder_60_cout, adder_60_out,
       adder_61_cout, adder_61_out, adder_62_cout, adder_62_out, adder_63_cout, adder_63_out, adder_64_cout,
       adder_64_out, adder_65_cout, adder_65_out, adder_66_cout, adder_66_out, adder_67_cout, adder_67_out,
       adder_68_cout, adder_68_out, adder_69_cout, adder_69_out, adder_70_cout, adder_70_out, adder_71_cout,
       adder_71_out, adder_72_cout, adder_72_out, and_1_out, and_2_out, and_3_out, and_4_out, and_5_out,
       and_6_out, and_7_out, and_8_out, and_9_out, and_10_out, and_11_out, and_12_out, and_13_out,
       and_14_out, and_15_out, and_16_out, and_17_out, and_18_out, and_19_out, and_20_out, and_21_out,
       and_22_out, and_23_out, and_24_out, and_25_out, and_26_out, and_27_out, and_28_out, and_29_out,
       and_30_out, and_31_out, and_32_out, and_33_out, and_34_out, and_35_out, and_36_out, and_37_out,
       and_38_out, and_39_out, and_40_out, and_41_out, and_42_out, and_43_out, and_44_out, and_45_out,
       and_46_out, and_47_out, and_48_out, and_49_out, and_50_out, and_51_out, and_52_out, and_53_out,
       and_54_out, and_55_out, and_56_out, and_57_out, and_58_out, and_59_out, and_60_out, and_61_out,
       and_62_out, and_63_out, and_64_out, clock_1_out, multiplexer_1_out, not_1_out, not_2_out,
       shift_register_1_out, shift_register_2_out, shift_register_3_q0, shift_register_3_q1,
       shift_register_3_q2, shift_register_3_q3, shift_register_3_q4, shift_register_3_q5,
       shift_register_3_q6, shift_register_3_q7, shift_register_4_out, shift_register_5_q0,
       shift_register_5_q1, shift_register_5_q2, shift_register_5_q3, shift_register_5_q4,
       shift_register_5_q5, shift_register_5_q6, shift_register_5_q7;

  Clock clock_1 (.out(clock_1_out));
  Shift_Register shift_register_1 (
    .shift(1'b1), .in(clock_1_out), .clk(clock_1_out), .out(shift_register_1_out), .clr(Clear));  // open: load, d0, q0, d1, q1, d2, q2, d3, q3, d4, q4, d5, q5, d6, q6, d7, q7
  Shift_Register #(.length(2)) shift_register_2 (
    .shift(1'b1), .in(shift_register_1_out), .clk(clock_1_out), .out(shift_register_2_out), .clr(Clear));  // open: load, d0, q0, d1, q1
  Adder #(.width(1)) adder_1 (.a(adder_2_cout), .b(1'b0), .out(adder_1_out), .cin(adder_3_cout));  // open: cout
  not not_1 (not_1_out, shift_register_1_out);
  Shift_Register shift_register_3 (
    .shift(not_1_out), .in(Serial_Multiplier), .clk(clock_1_out), .clr(Clear), .q0(shift_register_3_q0),
    .q1(shift_register_3_q1), .q2(shift_register_3_q2), .q3(shift_register_3_q3), .q4(shift_register_3_q4),
    .q5(shift_register_3_q5), .q6(shift_register_3_q6), .q7(shift_register_3_q7));  // open: out, load, d0, d1, d2, d3, d4, d5, d6, d7
  and and_1 (and_1_out, shift_register_3_q0, shift_register_5_q0);
  Adder #(.width(1)) adder_2 (.a(1'b0), .b(and_1_out), .out(adder_2_out), .cin(adder_4_cout), .cout(adder_2_cout));
  Adder #(.width(1)) adder_3 (
    .a(adder_5_cout), .b(adder_2_out), .out(adder_3_out), .cin(adder_6_cout), .cout(adder_3_cout));
  and and_2 (and_2_out, shift_register_3_q1, shift_register_5_q0);
  and and_3 (and_3_out, shift_register_3_q0, shift_register_5_q1);
  Multiplexer multiplexer_1 (
    .in0(shift_register_1_out), .in1(1'b0), .out(multiplexer_1_out), .sel(shift_register_2_out));  // open: en
  Adder #(.width(1)) adder_4 (.a(1'b0), .b(and_2_out), .out(adder_4_out), .cin(adder_7_cout), .cout(adder_4_cout));
  Adder #(.width(1)) adder_5 (
    .a(adder_4_out), .b(and_3_out), .out(adder_5_out), .cin(adder_8_cout), .cout(adder_5_cout));
  Adder #(.width(1)) adder_6 (
    .a(adder_9_cout), .b(adder_5_out), .out(adder_6_out), .cin(adder_10_cout), .cout(adder_6_cout));
  and and_4 (and_4_out, shift_register_3_q2, shift_register_5_q0);
  Adder #(.width(1)) adder_7 (.a(1'b0), .b(and_4_out), .out(adder_7_out), .cin(adder_11_cout), .cout(adder_7_cout));
  and and_5 (and_5_out, shift_register_3_q1, shift_register_5_q1);
  Adder #(.width(1)) adder_8 (
    .a(adder_7_out), .b(and_5_out), .out(adder_8_out), .cin(adder_12_cout), .cout(adder_8_cout));
  and and_6 (and_6_out, shift_register_3_q0, shift_register_5_q2);
  Adder #(.width(1)) adder_9 (
    .a(adder_8_out), .b(and_6_out), .out(adder_9_out), .cin(adder_13_cout), .cout(adder_9_cout));
  Adder #(.width(1)) adder_10 (
    .a(adder_14_cout), .b(adder_9_out), .out(adder_10_out), .cin(adder_15_cout), .cout(adder_10_cout));
  and and_7 (and_7_out, shift_register_3_q3, shift_register_5_q0);
  Adder #(.width(1)) adder_11 (.a(1'b0), .b(and_7_out), .out(adder_11_out), .cin(adder_16_cout), .cout(adder_11_cout));
  and and_8 (and_8_out, shift_register_3_q2, shift_register_5_q1);
  and and_9 (and_9_out, shift_register_3_q1, shift_register_5_q2);
  and and_10 (and_10_out, shift_register_3_q0, shift_register_5_q3);
  not not_2 (not_2_out, multiplexer_1_out);
  Shift_Register #(.length(16)) shift_register_4 (
    .shift(not_2_out), .clk(clock_1_out), .out(shift_register_4_out), .load(multiplexer_1_out), .clr(Clear),
    .d0(adder_1_out), .d1(adder_3_out), .d2(adder_6_out), .d3(adder_10_out), .d4(adder_15_out),
    .d5(adder_21_out), .d6(adder_28_out), .d7(adder_36_out), .d8(adder_44_out), .d9(adder_51_out),
    .d10(adder_57_out), .d11(adder_62_out), .d12(adder_66_out), .d13(adder_69_out), .d14(adder_71_out),
    .d15(adder_72_out));  // open: in, q0, q1, q2, q3, q4, q5, q6, q7, q8, q9, q10, q11, q12, q13, q14, q15
  and and_11 (and_11_out, shift_register_3_q4, shift_register_5_q0);
  and and_12 (and_12_out, shift_register_3_q3, shift_register_5_q1);
  Adder #(.width(1)) adder_12 (
    .a(adder_11_out), .b(and_8_out), .out(adder_12_out), .cin(adder_17_cout), .cout(adder_12_cout));
  Adder #(.width(1)) adder_13 (
    .a(adder_12_out), .b(and_9_out), .out(adder_13_out), .cin(adder_18_cout), .cout(adder_13_cout));
  Adder #(.width(1)) adder_14 (
    .a(adder_13_out), .b(and_10_out), .out(adder_14_out), .cin(adder_19_cout), .cout(adder_14_cout));
  Adder #(.width(1)) adder_15 (
    .a(adder_20_cout), .b(adder_14_out), .out(adder_15_out), .cin(adder_21_cout), .cout(adder_15_cout));
  Adder #(.width(1)) adder_16 (.a(1'b0), .b(and_11_out), .out(adder_16_out), .cin(adder_22_cout), .cout(adder_16_cout));
  Adder #(.width(1)) adder_17 (
    .a(adder_16_out), .b(and_12_out), .out(adder_17_out), .cin(adder_23_cout), .cout(adder_17_cout));
  and and_13 (and_13_out, shift_register_3_q2, shift_register_5_q2);
  Adder #(.width(1)) adder_18 (
    .a(adder_17_out), .b(and_13_out), .out(adder_18_out), .cin(adder_24_cout), .cout(adder_18_cout));
  and and_14 (and_14_out, shift_register_3_q1, shift_register_5_q3);
  Adder #(.width(1)) adder_19 (
    .a(adder_18_out), .b(and_14_out), .out(adder_19_out), .cin(adder_25_cout), .cout(adder_19_cout));
  and and_15 (and_15_out, shift_register_3_q0, shift_register_5_q4);
  Adder #(.width(1)) adder_20 (
    .a(adder_19_out), .b(and_15_out), .out(adder_20_out), .cin(adder_26_cout), .cout(adder_20_cout));
  Adder #(.width(1)) adder_21 (
    .a(adder_27_cout), .b(adder_20_out), .out(adder_21_out), .cin(adder_28_cout), .cout(adder_21_cout));
  and and_16 (and_16_out, shift_register_3_q5, shift_register_5_q0);
  Adder #(.width(1)) adder_22 (.a(1'b0), .b(and_16_out), .out(adder_22_out), .cin(adder_29_cout), .cout(adder_22_cout));
  and and_17 (and_17_out, shift_register_3_q4, shift_register_5_q1);
  Adder #(.width(1)) adder_23 (
    .a(adder_22_out), .b(and_17_out), .out(adder_23_out), .cin(adder_30_cout), .cout(adder_23_cout));
  and and_18 (and_18_out, shift_register_3_q3, shift_register_5_q2);
  Adder #(.width(1)) adder_24 (
    .a(adder_23_out), .b(and_18_out), .out(adder_24_out), .cin(adder_31_cout), .cout(adder_24_cout));
  and and_19 (and_19_out, shift_register_3_q2, shift_register_5_q3);
  and and_20 (and_20_out, shift_register_3_q1, shift_register_5_q4);
  and and_21 (and_21_out, shift_register_3_q0, shift_register_5_q5);
  and and_22 (and_22_out, shift_register_3_q6, shift_register_5_q0);
  and and_23 (and_23_out, shift_register_3_q5, shift_register_5_q1);
  and and_24 (and_24_out, shift_register_3_q4, shift_register_5_q2);
  and and_25 (and_25_out, shift_register_3_q3, shift_register_5_q3);
  Adder #(.width(1)) adder_25 (
    .a(adder_24_out), .b(and_19_out), .out(adder_25_out), .cin(adder_32_cout), .cout(adder_25_cout));
  Adder #(.width(1)) adder_26 (
    .a(adder_25_out), .b(and_20_out), .out(adder_26_out), .cin(adder_33_cout), .cout(adder_26_cout));
  Adder #(.width(1)) adder_27 (
    .a(adder_26_out), .b(and_21_out), .out(adder_27_out), .cin(adder_34_cout), .cout(adder_27_cout));
  Adder #(.width(1)) adder_28 (
    .a(adder_35_cout), .b(adder_27_out), .out(adder_28_out), .cin(adder_36_cout), .cout(adder_28_cout));
  Multiplexer multiplexer_2 (
    .in0(1'b0), .in1(shift_register_4_out), .out(out_4), .sel(shift_register_2_out));  // open: en
  Adder #(.width(1)) adder_29 (.a(1'b0), .b(and_22_out), .out(adder_29_out), .cin(adder_37_cout), .cout(adder_29_cout));
  Adder #(.width(1)) adder_30 (
    .a(adder_29_out), .b(and_23_out), .out(adder_30_out), .cin(adder_38_cout), .cout(adder_30_cout));
  Adder #(.width(1)) adder_31 (
    .a(adder_30_out), .b(and_24_out), .out(adder_31_out), .cin(adder_39_cout), .cout(adder_31_cout));
  Adder #(.width(1)) adder_32 (
    .a(adder_31_out), .b(and_25_out), .out(adder_32_out), .cin(adder_40_cout), .cout(adder_32_cout));
  and and_26 (and_26_out, shift_register_3_q2, shift_register_5_q4);
  Adder #(.width(1)) adder_33 (
    .a(adder_32_out), .b(and_26_out), .out(adder_33_out), .cin(adder_41_cout), .cout(adder_33_cout));
  and and_27 (and_27_out, shift_register_3_q1, shift_register_5_q5);
  Adder #(.width(1)) adder_34 (
    .a(adder_33_out), .b(and_27_out), .out(adder_34_out), .cin(adder_42_cout), .cout(adder_34_cout));
  and and_28 (and_28_out, shift_register_3_q0, shift_register_5_q6);
  Adder #(.width(1)) adder_35 (
    .a(adder_34_out), .b(and_28_out), .out(adder_35_out), .cin(adder_43_cout), .cout(adder_35_cout));
  Adder #(.width(1)) adder_36 (
    .a(adder_44_cout), .b(adder_35_out), .out(adder_36_out), .cin(1'b0), .cout(adder_36_cout));
  and and_29 (and_29_out, shift_register_3_q7, shift_register_5_q0);
  Adder #(.width(1)) adder_37 (.a(1'b0), .b(and_29_out), .out(adder_37_out), .cin(1'b0), .cout(adder_37_cout));
  and and_30 (and_30_out, shift_register_3_q6, shift_register_5_q1);
  Adder #(.width(1)) adder_38 (
    .a(adder_37_out), .b(and_30_out), .out(adder_38_out), .cin(adder_45_cout), .cout(adder_38_cout));
  and and_31 (and_31_out, shift_register_3_q5, shift_register_5_q2);
  Adder #(.width(1)) adder_39 (
    .a(adder_38_out), .b(and_31_out), .out(adder_39_out), .cin(adder_46_cout), .cout(adder_39_cout));
  and and_32 (and_32_out, shift_register_3_q4, shift_register_5_q3);
  Adder #(.width(1)) adder_40 (
    .a(adder_39_out), .b(and_32_out), .out(adder_40_out), .cin(adder_47_cout), .cout(adder_40_cout));
  and and_33 (and_33_out, shift_register_3_q3, shift_register_5_q4);
  and and_34 (and_34_out, shift_register_3_q2, shift_register_5_q5);
  and and_35 (and_35_out, shift_register_3_q1, shift_register_5_q6);
  and and_36 (and_36_out, shift_register_3_q0, shift_register_5_q7);
  and and_37 (and_37_out, shift_register_3_q6, shift_register_5_q2);
  and and_38 (and_38_out, shift_register_3_q5, shift_register_5_q3);
  Adder #(.width(1)) adder_41 (
    .a(adder_40_out), .b(and_33_out), .out(adder_41_out), .cin(adder_48_cout), .cout(adder_41_cout));
  Adder #(.width(1)) adder_42 (
    .a(adder_41_out), .b(and_34_out), .out(adder_42_out), .cin(adder_49_cout), .cout(adder_42_cout));
  Adder #(.width(1)) adder_43 (
    .a(adder_42_out), .b(and_35_out), .out(adder_43_out), .cin(adder_50_cout), .cout(adder_43_cout));
  Adder #(.width(1)) adder_44 (
    .a(adder_43_out), .b(and_36_out), .out(adder_44_out), .cin(adder_51_cout), .cout(adder_44_cout));
  and and_39 (and_39_out, shift_register_3_q7, shift_register_5_q1);
  Adder #(.width(1)) adder_45 (.a(1'b0), .b(and_39_out), .out(adder_45_out), .cin(1'b0), .cout(adder_45_cout));
  Adder #(.width(1)) adder_46 (
    .a(adder_45_out), .b(and_37_out), .out(adder_46_out), .cin(adder_53_cout), .cout(adder_46_cout));
  Adder #(.width(1)) adder_47 (
    .a(adder_46_out), .b(and_38_out), .out(adder_47_out), .cin(adder_52_cout), .cout(adder_47_cout));
  and and_40 (and_40_out, shift_register_3_q4, shift_register_5_q4);
  Adder #(.width(1)) adder_48 (
    .a(adder_47_out), .b(and_40_out), .out(adder_48_out), .cin(adder_54_cout), .cout(adder_48_cout));
  and and_41 (and_41_out, shift_register_3_q3, shift_register_5_q5);
  Adder #(.width(1)) adder_49 (
    .a(adder_48_out), .b(and_41_out), .out(adder_49_out), .cin(adder_55_cout), .cout(adder_49_cout));
  and and_42 (and_42_out, shift_register_3_q2, shift_register_5_q6);
  Adder #(.width(1)) adder_50 (
    .a(adder_49_out), .b(and_42_out), .out(adder_50_out), .cin(adder_56_cout), .cout(adder_50_cout));
  and and_43 (and_43_out, shift_register_3_q1, shift_register_5_q7);
  Adder #(.width(1)) adder_51 (
    .a(adder_50_out), .b(and_43_out), .out(adder_51_out), .cin(adder_57_cout), .cout(adder_51_cout));
  and and_44 (and_44_out, shift_register_3_q7, shift_register_5_q2);
  and and_45 (and_45_out, shift_register_3_q6, shift_register_5_q3);
  Adder #(.width(1)) adder_52 (
    .a(adder_53_out), .b(and_45_out), .out(adder_52_out), .cin(adder_58_cout), .cout(adder_52_cout));
  and and_46 (and_46_out, shift_register_3_q5, shift_register_5_q4);
  and and_47 (and_47_out, shift_register_3_q4, shift_register_5_q5);
  and and_48 (and_48_out, shift_register_3_q3, shift_register_5_q6);
  and and_49 (and_49_out, shift_register_3_q2, shift_register_5_q7);
  Adder #(.width(1)) adder_53 (.a(1'b0), .b(and_44_out), .out(adder_53_out), .cin(1'b0), .cout(adder_53_cout));
  Adder #(.width(1)) adder_54 (
    .a(adder_52_out), .b(and_46_out), .out(adder_54_out), .cin(adder_59_cout), .cout(adder_54_cout));
  Adder #(.width(1)) adder_55 (
    .a(adder_54_out), .b(and_47_out), .out(adder_55_out), .cin(adder_60_cout), .cout(adder_55_cout));
  Adder #(.width(1)) adder_56 (
    .a(adder_55_out), .b(and_48_out), .out(adder_56_out), .cin(adder_61_cout), .cout(adder_56_cout));
  Adder #(.width(1)) adder_57 (
    .a(adder_56_out), .b(and_49_out), .out(adder_57_out), .cin(adder_62_cout), .cout(adder_57_cout));
  Shift_Register shift_register_5 (
    .shift(not_1_out), .in(Serial_Multiplicand), .clk(clock_1_out), .clr(Clear), .q0(shift_register_5_q0),
    .q1(shift_register_5_q1), .q2(shift_register_5_q2), .q3(shift_register_5_q3), .q4(shift_register_5_q4),
    .q5(shift_register_5_q5), .q6(shift_register_5_q6), .q7(shift_register_5_q7));  // open: out, load, d0, d1, d2, d3, d4, d5, d6, d7
  and and_50 (and_50_out, shift_register_3_q7, shift_register_5_q3);
  Adder #(.width(1)) adder_58 (.a(1'b0), .b(and_50_out), .out(adder_58_out), .cin(1'b0), .cout(adder_58_cout));
  and and_51 (and_51_out, shift_register_3_q6, shift_register_5_q4);
  Adder #(.width(1)) adder_59 (
    .a(adder_58_out), .b(and_51_out), .out(adder_59_out), .cin(adder_63_cout), .cout(adder_59_cout));
  and and_52 (and_52_out, shift_register_3_q5, shift_register_5_q5);
  Adder #(.width(1)) adder_60 (
    .a(adder_59_out), .b(and_52_out), .out(adder_60_out), .cin(adder_64_cout), .cout(adder_60_cout));
  and and_53 (and_53_out, shift_register_3_q4, shift_register_5_q6);
  Adder #(.width(1)) adder_61 (
    .a(adder_60_out), .b(and_53_out), .out(adder_61_out), .cin(adder_65_cout), .cout(adder_61_cout));
  and and_54 (and_54_out, shift_register_3_q3, shift_register_5_q7);
  Adder #(.width(1)) adder_62 (
    .a(adder_61_out), .b(and_54_out), .out(adder_62_out), .cin(adder_66_cout), .cout(adder_62_cout));
  and and_55 (and_55_out, shift_register_3_q7, shift_register_5_q4);
  and and_56 (and_56_out, shift_register_3_q6, shift_register_5_q5);
  and and_57 (and_57_out, shift_register_3_q5, shift_register_5_q6);
  and and_58 (and_58_out, shift_register_3_q4, shift_register_5_q7);
  Adder #(.width(1)) adder_63 (.a(1'b0), .b(and_55_out), .out(adder_63_out), .cin(1'b0), .cout(adder_63_cout));
  Adder #(.width(1)) adder_64 (
    .a(adder_63_out), .b(and_56_out), .out(adder_64_out), .cin(adder_67_cout), .cout(adder_64_cout));
  Adder #(.width(1)) adder_65 (
    .a(adder_64_out), .b(and_57_out), .out(adder_65_out), .cin(adder_68_cout), .cout(adder_65_cout));
  Adder #(.width(1)) adder_66 (
    .a(adder_65_out), .b(and_58_out), .out(adder_66_out), .cin(adder_69_cout), .cout(adder_66_cout));
  and and_59 (and_59_out, shift_register_3_q7, shift_register_5_q5);
  Adder #(.width(1)) adder_67 (.a(1'b0), .b(and_59_out), .out(adder_67_out), .cin(1'b0), .cout(adder_67_cout));
  and and_60 (and_60_out, shift_register_3_q6, shift_register_5_q6);
  Adder #(.width(1)) adder_68 (
    .a(adder_67_out), .b(and_60_out), .out(adder_68_out), .cin(adder_70_cout), .cout(adder_68_cout));
  and and_61 (and_61_out, shift_register_3_q5, shift_register_5_q7);
  Adder #(.width(1)) adder_69 (
    .a(adder_68_out), .b(and_61_out), .out(adder_69_out), .cin(adder_71_cout), .cout(adder_69_cout));
  and and_62 (and_62_out, shift_register_3_q7, shift_register_5_q6);
  and and_63 (and_63_out, shift_register_3_q6, shift_register_5_q7);
  Adder #(.width(1)) adder_70 (.a(1'b0), .b(and_62_out), .out(adder_70_out), .cin(1'b0), .cout(adder_70_cout));
  Adder #(.width(1)) adder_71 (
    .a(adder_70_out), .b(and_63_out), .out(adder_71_out), .cin(adder_72_cout), .cout(adder_71_cout));
  and and_64 (and_64_out, shift_register_3_q7, shift_register_5_q7);
  Adder #(.width(1)) adder_72 (.a(1'b0), .b(and_64_out), .out(adder_72_out), .cin(1'b0), .cout(adder_72_cout));

  // Notes on the sheet:
  //   Delay register
  //   (for the purpose
  //   of reading output
  //   then shifting)
  //   "end input"
  //   register
  //   MUX that switches output reg from read output to shift mode
  //   Valid result multiplexer
endmodule
